# Fritzing sketch Effect-O-Matic (saved by Fritzing 0.7.7b)

parts:
  DB237 = NPN-Transistor [package="TO92 [THT]"]
  DB237_2 = NPN-Transistor [package="TO92 [THT]"]
  DB237_3 = NPN-Transistor [package="TO92 [THT]"]
  DB237_4 = NPN-Transistor [package="TO92 [THT]"]
  DB237_5 = NPN-Transistor [package="TO92 [THT]"]
  part = Resistor [tolerance=±5% resistance=1k package=THT]
  part_2 = Resistor [tolerance=±5% resistance=1k package=THT]
  part_3 = Resistor [tolerance=±5% resistance=1k package=THT]
  part_4 = Resistor [tolerance=±5% resistance=1k package=THT]
  IN = screw terminal, 7 pins
  part_5 = Resistor [tolerance=±5% resistance=1k package=THT]
  OUT = screw terminal, 6 pins
  Arduino = Arduino
  Controll_board = screw terminal, 7 pins

nets:
  GND: DB237.E, DB237_2.E, DB237_3.E, DB237_4.E, DB237_5.E, IN.pin2, Arduino.GND, Controll_board.pin2
  N1: DB237.B, part_2.Pin_0
  N2: DB237.C, OUT.pin1
  N3: DB237_2.B, part_5.Pin_0
  N4: DB237_2.C, OUT.pin2
  N5: DB237_3.B, part_3.Pin_0
  N6: DB237_3.C, OUT.pin3
  N7: DB237_4.B, part.Pin_0
  N8: DB237_4.C, OUT.pin4
  N9: DB237_5.B, part_4.Pin_0
  N10: DB237_5.C, OUT.pin5
  N11: part.Pin_1, IN.pin4
  N12: part_2.Pin_1, IN.pin7
  N13: part_3.Pin_1, IN.pin5
  N14: part_4.Pin_1, IN.pin3
  N15: IN.pin1, OUT.pin6
  N16: IN.pin6, part_5.Pin_1
  N17: Arduino.D10, Controll_board.pin7
  N18: Arduino.D9, Controll_board.pin6
  N19: Arduino.D6, Controll_board.pin5
  N20: Arduino.D5, Controll_board.pin4
  N21: Arduino.D3, Controll_board.pin3
  12V: Controll_board.pin1

notes:
  Input
  5
  4
  3
  2
  1
  -
  +12V
  Output
  5
  4
  3
  2
  1
  +12V
